// Digital circuit led_matrix.dig as structural Verilog
module led_matrix (
  input  clk,
  input  in_2,
  input  clk_2
);

  wire _6bit_shiftregister_1_p2, _6bit_shiftregister_1_p4, _6bit_shiftregister_1_p5,
       _6bit_shiftregister_1_p6, _6bit_shiftregister_1_p7, _6bit_shiftregister_1_p8,
       _6bit_shiftregister_1_p9, _6bit_shiftregister_1_p10, _6bit_shiftregister_1_p11,
       _6bit_shiftregister_1_p12, _6bit_shiftregister_1_p13, _6bit_shiftregister_1_p14,
       _6bit_shiftregister_1_p15, _6bit_shiftregister_1_p16, _6bit_shiftregister_1_p17,
       _6bit_shiftregister_1_p18, _6bit_shiftregister_1_p19, _6bit_shiftregister_1_p20,
       _6bit_shiftregister_1_p21, _6bit_shiftregister_1_p22, _6bit_shiftregister_1_p23,
       _6bit_shiftregister_1_p24, _6bit_shiftregister_1_p25, _6bit_shiftregister_1_p26,
       _6bit_shiftregister_1_p27, _6bit_shiftregister_1_p28, undriven, undriven_2, undriven_3, undriven_4,
       undriven_5, undriven_6, undriven_7, undriven_8, undriven_9, undriven_10, undriven_11, undriven_12,
       undriven_13, undriven_14, undriven_15, undriven_16, undriven_17, undriven_18, undriven_19,
       undriven_20, undriven_21, undriven_22, undriven_23, undriven_24, undriven_25, undriven_26,
       undriven_27, undriven_28, undriven_29, undriven_30, undriven_31, undriven_32, undriven_33,
       undriven_34, undriven_35, undriven_36, undriven_37, undriven_38, undriven_39, undriven_40,
       undriven_41, undriven_42, undriven_43, undriven_44, undriven_45, undriven_46, undriven_47,
       undriven_48, undriven_49, undriven_50, undriven_51, undriven_52, undriven_53, undriven_54,
       undriven_55, undriven_56, undriven_57, undriven_58, undriven_59, undriven_60, undriven_61,
       undriven_62, undriven_63, undriven_64, undriven_65, undriven_66, undriven_67, undriven_68,
       undriven_69, undriven_70, undriven_71, undriven_72, undriven_73, undriven_74, undriven_75,
       undriven_76, undriven_77, undriven_78, undriven_79, undriven_80, undriven_81, undriven_82,
       undriven_83, undriven_84, undriven_85, undriven_86, undriven_87, undriven_88, undriven_89,
       undriven_90, undriven_91, undriven_92, undriven_93, undriven_94, undriven_95, undriven_96,
       undriven_97, undriven_98, undriven_99, undriven_100, undriven_101, undriven_102, undriven_103,
       undriven_104, undriven_105, undriven_106, undriven_107, undriven_108, undriven_109, undriven_110,
       undriven_111, undriven_112, undriven_113, undriven_114, undriven_115, undriven_116, undriven_117,
       undriven_118, undriven_119, undriven_120, undriven_121, undriven_122, undriven_123, undriven_124,
       undriven_125, undriven_126, undriven_127, undriven_128, undriven_131, undriven_132, undriven_133,
       undriven_134, undriven_135, undriven_136, undriven_137, undriven_138, undriven_139, undriven_140,
       undriven_141, undriven_142, undriven_143, undriven_144, undriven_145, undriven_146, undriven_147,
       undriven_148, undriven_149, undriven_150, undriven_151, undriven_152, undriven_153, undriven_154,
       undriven_155, undriven_156, undriven_157, undriven_158, undriven_159, undriven_160, undriven_161,
       undriven_162;
  wire [5:0] d_ff_1_q, u_counter_c;
  wire [6:0] _6bit_shiftregister_1_p1;
  wire [18:0] u_control_circuit_ledout;
  wire [19:0] undriven_129, undriven_130;

  control_circuit #(.applicationType("GHDL")) u_control_circuit (
    .Reset(in_2), .clk(clk), .LEDout(u_control_circuit_ledout[15:0]));
  control_circuit #(.applicationType("GHDL")) u_control_circuit_2 ();  // open: clk, jump, squat, Reset, Display15, Display14, Display13, Display12, Display11, Display10, Display9, Display8, Display7, Display6, Display5, Display4, Display3, Display2, Display1, Display0, over
  counter #(.applicationType("GHDL")) u_counter (.clk(clk_2), .c(u_counter_c));
  D_FF #(.Bits(6)) d_ff_1 (.D(u_counter_c), .Q(d_ff_1_q));  // open: C, nQ
  // _6bit_ShiftRegister _6bit_shiftregister_1: pin names not known; wires that end beside it: _6bit_shiftregister_1_p1, _6bit_shiftregister_1_p2, d_ff_1_q, _6bit_shiftregister_1_p4, _6bit_shiftregister_1_p5, _6bit_shiftregister_1_p6, _6bit_shiftregister_1_p7, _6bit_shiftregister_1_p8, _6bit_shiftregister_1_p9, _6bit_shiftregister_1_p10, _6bit_shiftregister_1_p11, _6bit_shiftregister_1_p12, _6bit_shiftregister_1_p13, _6bit_shiftregister_1_p14, _6bit_shiftregister_1_p15, _6bit_shiftregister_1_p16, _6bit_shiftregister_1_p17, _6bit_shiftregister_1_p18, _6bit_shiftregister_1_p19, _6bit_shiftregister_1_p20, _6bit_shiftregister_1_p21, _6bit_shiftregister_1_p22, _6bit_shiftregister_1_p23, _6bit_shiftregister_1_p24, _6bit_shiftregister_1_p25, _6bit_shiftregister_1_p26, _6bit_shiftregister_1_p27, _6bit_shiftregister_1_p28
  LED led_1 (.in(undriven));
  LED led_2 (.in(undriven_2));
  LED led_3 (.in(undriven_3));
  LED led_4 (.in(undriven_4));
  LED led_5 (.in(undriven_129[19]));
  LED led_6 ();  // open: in
  LED led_7 (.in(undriven_130[19]));
  LED led_8 (.in(_6bit_shiftregister_1_p8));
  LED led_9 ();  // open: in
  LED led_10 (.in(undriven_8));
  LED led_11 (.in(undriven_5));
  LED led_12 (.in(undriven_9));
  LED led_13 (.in(undriven_6));
  LED led_14 (.in(undriven_10));
  LED led_15 (.in(undriven_7));
  LED led_16 (.in(undriven_11));
  LED led_17 (.in(undriven_129[18]));
  LED led_18 (.in(undriven_129[17]));
  LED led_19 ();  // open: in
  LED led_20 ();  // open: in
  LED led_21 (.in(undriven_130[18]));
  LED led_22 (.in(undriven_130[17]));
  LED led_23 (.in(_6bit_shiftregister_1_p11));
  LED led_24 ();  // open: in
  LED led_25 (.in(undriven_17));
  LED led_26 (.in(undriven_18));
  LED led_27 (.in(undriven_12));
  LED led_28 (.in(undriven_19));
  LED led_29 (.in(undriven_13));
  LED led_30 (.in(undriven_20));
  LED led_31 (.in(undriven_14));
  LED led_32 (.in(undriven_15));
  LED led_33 (.in(undriven_129[16]));
  LED led_34 (.in(undriven_129[15]));
  LED led_35 (.in(undriven_16));
  LED led_36 ();  // open: in
  LED led_37 (.in(undriven_130[16]));
  LED led_38 (.in(undriven_130[15]));
  LED led_39 ();  // open: in
  LED led_40 ();  // open: in
  LED led_41 (.in(undriven_21));
  LED led_42 (.in(undriven_25));
  LED led_43 (.in(undriven_22));
  LED led_44 (.in(undriven_26));
  LED led_45 (.in(undriven_23));
  LED led_46 (.in(undriven_27));
  LED led_47 (.in(undriven_24));
  LED led_48 (.in(undriven_28));
  LED led_49 (.in(undriven_129[14]));
  LED led_50 (.in(undriven_129[13]));
  LED led_51 ();  // open: in
  LED led_52 ();  // open: in
  LED led_53 (.in(undriven_130[14]));
  LED led_54 (.in(undriven_130[13]));
  LED led_55 ();  // open: in
  LED led_56 ();  // open: in
  LED led_57 (.in(undriven_29));
  LED led_58 (.in(undriven_30));
  LED led_59 (.in(undriven_31));
  LED led_60 (.in(undriven_32));
  LED led_61 (.in(_6bit_shiftregister_1_p22));
  LED led_62 (.in(_6bit_shiftregister_1_p23));
  LED led_63 (.in(_6bit_shiftregister_1_p24));
  LED led_64 (.in(undriven_33));
  LED led_65 (.in(undriven_41));
  LED led_66 (.in(undriven_34));
  LED led_67 (.in(undriven_42));
  LED led_68 (.in(undriven_35));
  LED led_69 (.in(undriven_43));
  LED led_70 (.in(undriven_36));
  LED led_71 (.in(undriven_44));
  LED led_72 (.in(undriven_129[12]));
  LED led_73 (.in(undriven_129[11]));
  LED led_74 ();  // open: in
  LED led_75 ();  // open: in
  LED led_76 (.in(undriven_130[12]));
  LED led_77 (.in(undriven_130[11]));
  LED led_78 ();  // open: in
  LED led_79 ();  // open: in
  LED led_80 (.in(undriven_37));
  LED led_81 (.in(undriven_45));
  LED led_82 (.in(undriven_38));
  LED led_83 (.in(undriven_46));
  LED led_84 (.in(undriven_39));
  LED led_85 (.in(undriven_47));
  LED led_86 (.in(undriven_40));
  LED led_87 (.in(undriven_48));
  LED led_88 (.in(_6bit_shiftregister_1_p26));
  LED led_89 (.in(_6bit_shiftregister_1_p28));
  LED led_90 (.in(_6bit_shiftregister_1_p27));
  LED led_91 ();  // open: in
  LED led_92 ();  // open: in
  LED led_93 ();  // open: in
  LED led_94 (.in(undriven_49));
  LED led_95 (.in(undriven_53));
  LED led_96 (.in(undriven_50));
  LED led_97 (.in(undriven_54));
  LED led_98 (.in(undriven_51));
  LED led_99 (.in(undriven_55));
  LED led_100 (.in(undriven_52));
  LED led_101 (.in(undriven_56));
  LED led_102 (.in(undriven_129[10]));
  LED led_103 (.in(undriven_129[9]));
  LED led_104 ();  // open: in
  LED led_105 ();  // open: in
  LED led_106 (.in(undriven_130[10]));
  LED led_107 (.in(undriven_130[9]));
  LED led_108 ();  // open: in
  LED led_109 ();  // open: in
  LED led_110 (.in(_6bit_shiftregister_1_p1[6]));
  LED led_111 (.in(undriven_57));
  LED led_112 (.in(undriven_58));
  LED led_113 (.in(_6bit_shiftregister_1_p1[5]));
  LED led_114 (.in(undriven_59));
  LED led_115 (.in(_6bit_shiftregister_1_p1[4]));
  LED led_116 (.in(undriven_60));
  LED led_117 (.in(_6bit_shiftregister_1_p1[3]));
  LED led_118 ();  // open: in
  LED led_119 (.in(_6bit_shiftregister_1_p1[2]));
  LED led_120 (.in(_6bit_shiftregister_1_p1[1]));
  LED led_121 ();  // open: in
  LED led_122 (.in(_6bit_shiftregister_1_p1[0]));
  LED led_123 ();  // open: in
  LED led_124 (.in(undriven_61));
  LED led_125 (.in(undriven_69));
  LED led_126 (.in(undriven_62));
  LED led_127 (.in(undriven_70));
  LED led_128 (.in(undriven_63));
  LED led_129 (.in(undriven_71));
  LED led_130 (.in(undriven_64));
  LED led_131 (.in(undriven_72));
  LED led_132 (.in(undriven_129[8]));
  LED led_133 (.in(undriven_129[7]));
  LED led_134 ();  // open: in
  LED led_135 ();  // open: in
  LED led_136 (.in(undriven_130[8]));
  LED led_137 (.in(undriven_130[7]));
  LED led_138 ();  // open: in
  LED led_139 ();  // open: in
  LED led_140 (.in(undriven_65));
  LED led_141 (.in(undriven_73));
  LED led_142 (.in(undriven_66));
  LED led_143 (.in(undriven_74));
  LED led_144 (.in(undriven_67));
  LED led_145 (.in(undriven_75));
  LED led_146 (.in(undriven_68));
  LED led_147 (.in(undriven_76));
  LED led_148 ();  // open: in
  LED led_149 ();  // open: in
  LED led_150 ();  // open: in
  LED led_151 ();  // open: in
  LED led_152 ();  // open: in
  LED led_153 ();  // open: in
  LED led_154 (.in(undriven_77));
  LED led_155 (.in(undriven_85));
  LED led_156 (.in(undriven_78));
  LED led_157 (.in(undriven_86));
  LED led_158 (.in(undriven_79));
  LED led_159 (.in(undriven_87));
  LED led_160 (.in(undriven_80));
  LED led_161 (.in(undriven_88));
  LED led_162 (.in(undriven_129[6]));
  LED led_163 (.in(undriven_129[5]));
  LED led_164 ();  // open: in
  LED led_165 ();  // open: in
  LED led_166 (.in(undriven_130[6]));
  LED led_167 (.in(undriven_130[5]));
  LED led_168 ();  // open: in
  LED led_169 ();  // open: in
  LED led_170 (.in(undriven_81));
  LED led_171 (.in(undriven_89));
  LED led_172 (.in(undriven_82));
  LED led_173 (.in(undriven_90));
  LED led_174 (.in(undriven_83));
  LED led_175 (.in(undriven_91));
  LED led_176 (.in(undriven_84));
  LED led_177 (.in(undriven_92));
  LED led_178 ();  // open: in
  LED led_179 ();  // open: in
  LED led_180 ();  // open: in
  LED led_181 ();  // open: in
  LED led_182 ();  // open: in
  LED led_183 ();  // open: in
  LED led_184 (.in(undriven_93));
  LED led_185 (.in(undriven_101));
  LED led_186 (.in(undriven_94));
  LED led_187 (.in(undriven_102));
  LED led_188 (.in(undriven_95));
  LED led_189 (.in(undriven_103));
  LED led_190 (.in(undriven_96));
  LED led_191 (.in(undriven_104));
  LED led_192 (.in(undriven_129[4]));
  LED led_193 (.in(undriven_129[3]));
  LED led_194 ();  // open: in
  LED led_195 ();  // open: in
  LED led_196 (.in(undriven_130[4]));
  LED led_197 (.in(undriven_130[3]));
  LED led_198 ();  // open: in
  LED led_199 ();  // open: in
  LED led_200 (.in(undriven_97));
  LED led_201 (.in(undriven_105));
  LED led_202 (.in(undriven_98));
  LED led_203 (.in(undriven_106));
  LED led_204 (.in(undriven_99));
  LED led_205 (.in(undriven_107));
  LED led_206 (.in(undriven_100));
  LED led_207 (.in(undriven_108));
  LED led_208 ();  // open: in
  LED led_209 ();  // open: in
  LED led_210 ();  // open: in
  LED led_211 ();  // open: in
  LED led_212 ();  // open: in
  LED led_213 ();  // open: in
  LED led_214 (.in(undriven_109));
  LED led_215 (.in(undriven_117));
  LED led_216 (.in(undriven_110));
  LED led_217 (.in(undriven_118));
  LED led_218 (.in(undriven_111));
  LED led_219 (.in(undriven_119));
  LED led_220 (.in(undriven_112));
  LED led_221 (.in(undriven_120));
  LED led_222 (.in(undriven_129[2]));
  LED led_223 (.in(undriven_129[1]));
  LED led_224 ();  // open: in
  LED led_225 ();  // open: in
  LED led_226 (.in(undriven_130[2]));
  LED led_227 (.in(undriven_130[1]));
  LED led_228 ();  // open: in
  LED led_229 ();  // open: in
  LED led_230 (.in(undriven_113));
  LED led_231 (.in(undriven_121));
  LED led_232 (.in(undriven_114));
  LED led_233 (.in(undriven_122));
  LED led_234 (.in(undriven_115));
  LED led_235 (.in(undriven_123));
  LED led_236 (.in(undriven_116));
  LED led_237 (.in(undriven_124));
  LED led_238 ();  // open: in
  LED led_239 ();  // open: in
  LED led_240 ();  // open: in
  LED led_241 ();  // open: in
  LED led_242 ();  // open: in
  LED led_243 ();  // open: in
  LED led_244 (.in(undriven_125));
  LED led_245 (.in(undriven_126));
  LED led_246 (.in(undriven_127));
  LED led_247 (.in(undriven_128));
  LED led_248 (.in(undriven_129[0]));
  LED led_249 ();  // open: in
  LED led_250 (.in(undriven_130[0]));
  LED led_251 ();  // open: in
  LED led_252 ();  // open: in
  LED led_253 (.in(undriven_131));
  LED led_254 (.in(undriven_135));
  LED led_255 (.in(undriven_132));
  LED led_256 (.in(undriven_136));
  LED led_257 (.in(undriven_133));
  LED led_258 (.in(undriven_137));
  LED led_259 (.in(undriven_134));
  LED led_260 (.in(undriven_138));
  LED led_261 ();  // open: in
  LED led_262 ();  // open: in
  LED led_263 ();  // open: in
  LED led_264 ();  // open: in
  LED led_265 ();  // open: in
  LED led_266 ();  // open: in
  LED led_267 (.in(undriven_139));
  LED led_268 (.in(undriven_143));
  LED led_269 (.in(undriven_140));
  LED led_270 (.in(undriven_144));
  LED led_271 (.in(undriven_141));
  LED led_272 (.in(undriven_145));
  LED led_273 (.in(undriven_142));
  LED led_274 (.in(undriven_146));
  LED led_275 ();  // open: in
  LED led_276 ();  // open: in
  LED led_277 ();  // open: in
  LED led_278 ();  // open: in
  LED led_279 ();  // open: in
  LED led_280 ();  // open: in
  LED led_281 (.in(undriven_147));
  LED led_282 (.in(undriven_151));
  LED led_283 (.in(undriven_148));
  LED led_284 (.in(undriven_152));
  LED led_285 (.in(undriven_149));
  LED led_286 (.in(undriven_153));
  LED led_287 (.in(undriven_150));
  LED led_288 (.in(undriven_154));
  LED led_289 ();  // open: in
  LED led_290 ();  // open: in
  LED led_291 ();  // open: in
  LED led_292 ();  // open: in
  LED led_293 ();  // open: in
  LED led_294 ();  // open: in
  LED led_295 (.in(undriven_155));
  LED led_296 (.in(undriven_159));
  LED led_297 (.in(undriven_156));
  LED led_298 (.in(undriven_160));
  LED led_299 (.in(undriven_157));
  LED led_300 (.in(undriven_161));
  LED led_301 (.in(undriven_158));
  LED led_302 (.in(undriven_162));
  LED led_303 ();  // open: in
  LED led_304 ();  // open: in
  LED led_305 ();  // open: in
  LED led_306 ();  // open: in
  LED led_307 ();  // open: in
  LED led_308 ();  // open: in
  // Pins of 16 and 19 bits meet at u_control_circuit_ledout

  // Notes on the sheet:
  //   clk_2: Hz: 10
endmodule

/* Code of control_circuit:
library ieee;
use ieee.std_logic_1164.all;
use ieee.numeric_std.all;

entity control_circuit is	
	port	(
		-- Input ports
		Reset, clk: in  std_logic;
		-- Output ports
		LEDout : out std_logic_vector(15 downto 0));
end control_circuit;

architecture state_graph of control_circuit is	
	signal pattern : std_logic_vector(15 downto 0) := "0000000000000001";	
begin
	LEDOUT <= pattern;
	process(CLK, RESET)
	begin
		if RESET = '1' then
			pattern <= "0000000000000001";
		elsif rising_edge(CLK) then
			pattern <= pattern(0) & pattern(15 downto 1);
		end if;
	end process;
end state_graph;
*/

/* Code of control_circuit:
library ieee;
use ieee.std_logic_1164.all;
use ieee.numeric_std.all;

entity control_circuit is	
	port	(
		-- Input ports
		clk, jump, squat, Reset: in  std_logic;
		-- Output ports
		Display15,Display14,Display13,Display12,Display11,Display10,Display9,Display8,Display7,Display6,Display5,Display4,Display3,Display2,Display1,Display0: out std_logic_vector(11 downto 0);		
		over : out std_logic);
end control_circuit;

architecture state_graph of control_circuit is	

---------------------------------------------------------------------------
type BGmemory is array (15 downto 0) of std_logic_vector(6 downto 0);
signal Space: BGmemory:=("0000000", "00000000","0000000","0000000","0000000","0000000","0000000","0000000","0000000","0000000","0000000","0000000","0000000","0000000","0000000","0000000");
signal MBSpace: BGmemory:=("0000000", "0000000","0000000","0000000","0000000","0000000","0000000","0000000","0000000","0000000","0000000","0000000","0000000","0000000","0000000","0000000");
---------------------------------------------------------------------------


	signal out_vector : std_logic_vector(3 downto 0) := "0000";
	signal state : std_logic_vector(3 downto 0):= "0000";
	
Begin
----------------------------------------------------
Display0 <= Space(0) or MBSpace(0);
Display1 <= Space(1) or MBSpace(1);
Display2 <= Space(2) or MBSpace(2);
Display3 <= Space(3) or MBSpace(3);
Display4 <= Space(4) or MBSpace(4);
Display5 <= Space(5) or MBSpace(5);
Display6 <= Space(6) or MBSpace(6);
Display7 <= Space(7) or MBSpace(7);
Display8 <= Space(8) or MBSpace(8);
Display9 <= Space(9) or MBSpace(9);
Display10 <= Space(10) or MBSpace(10);
Display11 <= Space(11) or MBSpace(11);
Display12 <= Space(12) or MBSpace(12);
Display13 <= Space(13) or MBSpace(13);
Display14 <= Space(14) or MBSpace(14);
Display15 <= Space(15) or MBSpace(15);


end state_graph;
*/

/* Code of counter:
library ieee;
use ieee.std_logic_1164.all;

entity counter is	
	port(
		-- Input ports
		clk: in std_logic;
		-- Output ports		
		c : out std_logic_vector(5 downto 0));
end counter;

architecture state_graph of counter is	
	signal z : std_logic_vector(5 downto 0) := "000000";
Begin
	c(5) <= z(5);
	c(4) <= z(4);
	c(3) <= z(3);
	c(2) <= z(2);
	c(1) <= z(1);
	c(0) <= z(0);

	process(clk) is
 	begin
 		if(rising_edge(clk)) then
			if(z = "000001") then z <= "000011";
			elsif(z = "000011") then z <= "000100";
			elsif(z = "000100") then z <= "000001";
			else z <= "000001";
			end if;
		end if;
	end process; 
end state_graph;
*/
