// Digital circuit main.dig as structural Verilog
module main (
  input  clk_2hz,
  input  [1:0] seed,
  input  clk_1hz,
  input  clk_5hz,
  input  clk_10hz,
  input  clk,
  input  clk_2,
  output [1:0] out_6,
  output [5:0] out_7
);

  wire DOWN_out, or_1_out, or_2_out, or_3_out, or_4_out, or_5_out, or_6_out, Replay_out, Start_out,
       u_BinaryToBCD_Score_clr, u_BinaryToBCD_Score_en, UP_out;
  wire [3:0] u_BinaryToBCD_Score_digit0, u_BinaryToBCD_Score_digit1, u_BinaryToBCD_Score_digit2,
       u_BinaryToBCD_Score_digit3;
  wire [5:0] u_control_circuit_player_display, u_control_circuit_q_signal;
  wire [6:0] u_SegDecoder_2_seg, u_SegDecoder_3_seg, u_SegDecoder_4_seg, u_SegDecoder_seg;
  wire [15:0] u_LEVEL_e, u_LEVEL_l, u_LEVEL_v, u_Q_qq, u_SCORE_c, u_SCORE_e, u_SCORE_o, u_SCORE_r, u_SCORE_s;
  wire [19:0] counter_1_out, u_control_circuit_display0, u_control_circuit_display1,
       u_control_circuit_display2, u_control_circuit_display3, u_control_circuit_display4,
       u_control_circuit_display5, u_control_circuit_ground, u_control_circuit_ground_fig;

  Button Start (.out(Start_out));
  Button Replay (.out(Replay_out));
  Button UP (.out(UP_out));
  Button DOWN (.out(DOWN_out));
  random random_1 (.clk(clk_1hz), .start(1'b1), .seed(seed), .stop(1'b0), .\rand (out_6));
  control_circuit #(.applicationType("GHDL")) u_control_circuit (
    .clk_1hz(clk_1hz), .clk_2hz(clk_2hz), .clk_5hz(clk_5hz), .clk_10hz(clk_10hz), .start(Start_out),
    .replay(Replay_out), .jump(UP_out), .squat(DOWN_out), .rand2(out_6[0]), .rand0(out_6[1]),
    .block_temp({u_control_circuit_display5[17], u_control_circuit_display4[17], u_control_circuit_display3[17], u_control_circuit_display2[17], u_control_circuit_display1[17], u_control_circuit_display0[17]}),
    .time_signal(out_7), .q_signal(u_control_circuit_q_signal), .ground(u_control_circuit_ground),
    .ground_fig(u_control_circuit_ground_fig), .display5(u_control_circuit_display5),
    .display4(u_control_circuit_display4), .display3(u_control_circuit_display3),
    .display2(u_control_circuit_display2), .display1(u_control_circuit_display1),
    .display0(u_control_circuit_display0), .player_display(u_control_circuit_player_display));
  SCORE #(.applicationType("GHDL")) u_SCORE (
    .On_Off(1'b1), .S(u_SCORE_s), .C(u_SCORE_c), .O(u_SCORE_o), .R(u_SCORE_r), .E(u_SCORE_e));
  LEVEL #(.applicationType("GHDL")) u_LEVEL (.On_Off(1'b1), .L(u_LEVEL_l), .E(u_LEVEL_e), .V(u_LEVEL_v));
  SixteenSeg sixteenseg_1 (.led(u_SCORE_s), .dp(1'b0));
  SixteenSeg sixteenseg_2 (.led(u_LEVEL_l), .dp(1'b0));
  or or_1 (or_1_out, u_control_circuit_display5[17], u_control_circuit_player_display[5]);
  or or_2 (or_2_out, u_control_circuit_display4[17], u_control_circuit_player_display[4]);
  or or_3 (or_3_out, u_control_circuit_display3[17], u_control_circuit_player_display[3]);
  or or_4 (or_4_out, u_control_circuit_display2[17], u_control_circuit_player_display[2]);
  or or_5 (or_5_out, u_control_circuit_display1[17], u_control_circuit_player_display[1]);
  or or_6 (or_6_out, u_control_circuit_display0[17], u_control_circuit_player_display[0]);
  SixteenSeg sixteenseg_3 (.led(u_SCORE_c), .dp(1'b0));
  SixteenSeg sixteenseg_4 (.led(u_LEVEL_e), .dp(1'b0));
  SixteenSeg sixteenseg_5 (.led(u_SCORE_o), .dp(1'b0));
  SixteenSeg sixteenseg_6 (.led(u_LEVEL_v), .dp(1'b0));
  LED led_1 (.in(u_control_circuit_display5[19]));
  LED led_2 (.in(u_control_circuit_display4[19]));
  LED led_3 (.in(u_control_circuit_display3[19]));
  LED led_4 (.in(u_control_circuit_display2[19]));
  LED led_5 (.in(u_control_circuit_display1[19]));
  LED led_6 (.in(u_control_circuit_display0[19]));
  // RGBLED rgbled_1: pin names not known; wires that end beside it: u_control_circuit_ground_fig[19], u_control_circuit_ground[19], 1'b0
  SixteenSeg sixteenseg_7 (.led(u_SCORE_r), .dp(1'b0));
  SixteenSeg sixteenseg_8 (.led(u_LEVEL_e), .dp(1'b0));
  LED led_7 (.in(u_control_circuit_display5[18]));
  LED led_8 (.in(u_control_circuit_display4[18]));
  LED led_9 (.in(u_control_circuit_display3[18]));
  LED led_10 (.in(u_control_circuit_display2[18]));
  LED led_11 (.in(u_control_circuit_display1[18]));
  LED led_12 (.in(u_control_circuit_display0[18]));
  // RGBLED rgbled_2: pin names not known; wires that end beside it: u_control_circuit_ground_fig[18], u_control_circuit_ground[18], 1'b0
  SixteenSeg sixteenseg_9 (.led(u_SCORE_e), .dp(1'b0));
  SixteenSeg sixteenseg_10 (.led(u_LEVEL_l), .dp(1'b0));
  LED led_13 (.in(or_1_out));
  LED led_14 (.in(or_2_out));
  LED led_15 (.in(or_3_out));
  LED led_16 (.in(or_4_out));
  LED led_17 (.in(or_5_out));
  LED led_18 (.in(or_6_out));
  // RGBLED rgbled_3: pin names not known; wires that end beside it: u_control_circuit_ground_fig[17], u_control_circuit_ground[17], 1'b0
  LED led_19 (.in(u_control_circuit_display5[16]));
  LED led_20 (.in(u_control_circuit_display4[16]));
  LED led_21 (.in(u_control_circuit_display3[16]));
  LED led_22 (.in(u_control_circuit_display2[16]));
  LED led_23 (.in(u_control_circuit_display1[16]));
  LED led_24 (.in(u_control_circuit_display0[16]));
  // RGBLED rgbled_4: pin names not known; wires that end beside it: u_control_circuit_ground_fig[16], u_control_circuit_ground[16], 1'b0
  SegDecoder #(.applicationType("GHDL")) u_SegDecoder (
    .Number(u_BinaryToBCD_Score_digit3), .up(1'b1), .Seg(u_SegDecoder_seg));  // open: down
  Q #(.applicationType("GHDL")) u_Q (.On_Off(1'b1), .clk(clk), .q_signal(u_control_circuit_q_signal), .qq(u_Q_qq));
  LED led_25 (.in(u_control_circuit_display5[15]));
  LED led_26 (.in(u_control_circuit_display4[15]));
  LED led_27 (.in(u_control_circuit_display3[15]));
  LED led_28 (.in(u_control_circuit_display2[15]));
  LED led_29 (.in(u_control_circuit_display1[15]));
  LED led_30 (.in(u_control_circuit_display0[15]));
  // RGBLED rgbled_5: pin names not known; wires that end beside it: u_control_circuit_ground_fig[15], u_control_circuit_ground[15], 1'b0
  Seven_Seg seven_seg_1 (
    .a(u_SegDecoder_seg[0]), .b(u_SegDecoder_seg[1]), .c(u_SegDecoder_seg[2]), .d(u_SegDecoder_seg[3]),
    .e(u_SegDecoder_seg[4]), .f(u_SegDecoder_seg[5]), .g(u_SegDecoder_seg[6]), .dp(1'b0));
  SixteenSeg sixteenseg_11 (.led(u_Q_qq), .dp(1'b0));
  LED led_31 (.in(u_control_circuit_display5[14]));
  LED led_32 (.in(u_control_circuit_display4[14]));
  LED led_33 (.in(u_control_circuit_display3[14]));
  LED led_34 (.in(u_control_circuit_display2[14]));
  LED led_35 (.in(u_control_circuit_display1[14]));
  LED led_36 (.in(u_control_circuit_display0[14]));
  // RGBLED rgbled_6: pin names not known; wires that end beside it: u_control_circuit_ground_fig[14], u_control_circuit_ground[14], 1'b0
  SegDecoder #(.applicationType("GHDL")) u_SegDecoder_2 (
    .Number(u_BinaryToBCD_Score_digit2), .up(1'b1), .Seg(u_SegDecoder_2_seg));  // open: down
  LED led_37 (.in(u_control_circuit_display5[13]));
  LED led_38 (.in(u_control_circuit_display4[13]));
  LED led_39 (.in(u_control_circuit_display3[13]));
  LED led_40 (.in(u_control_circuit_display2[13]));
  LED led_41 (.in(u_control_circuit_display1[13]));
  LED led_42 (.in(u_control_circuit_display0[13]));
  // RGBLED rgbled_7: pin names not known; wires that end beside it: u_control_circuit_ground_fig[13], u_control_circuit_ground[13], 1'b0
  Seven_Seg seven_seg_2 (
    .a(u_SegDecoder_2_seg[0]), .b(u_SegDecoder_2_seg[1]), .c(u_SegDecoder_2_seg[2]),
    .d(u_SegDecoder_2_seg[3]), .e(u_SegDecoder_2_seg[4]), .f(u_SegDecoder_2_seg[5]),
    .g(u_SegDecoder_2_seg[6]), .dp(1'b0));
  Counter #(.Bits(20)) counter_1 (
    .en(u_BinaryToBCD_Score_en), .C(clk_2), .clr(u_BinaryToBCD_Score_clr), .out(counter_1_out));  // open: ovf
  LED led_43 (.in(u_control_circuit_display5[12]));
  LED led_44 (.in(u_control_circuit_display4[12]));
  LED led_45 (.in(u_control_circuit_display3[12]));
  LED led_46 (.in(u_control_circuit_display2[12]));
  LED led_47 (.in(u_control_circuit_display1[12]));
  LED led_48 (.in(u_control_circuit_display0[12]));
  // RGBLED rgbled_8: pin names not known; wires that end beside it: u_control_circuit_ground_fig[12], u_control_circuit_ground[12], 1'b0
  SegDecoder #(.applicationType("GHDL")) u_SegDecoder_3 (
    .Number(u_BinaryToBCD_Score_digit1), .up(1'b1), .Seg(u_SegDecoder_3_seg));  // open: down
  BinaryToBCD_Score #(.applicationType("GHDL")) u_BinaryToBCD_Score (
    .Score(counter_1_out), .qq(u_control_circuit_q_signal), .Digit3(u_BinaryToBCD_Score_digit3),
    .Digit2(u_BinaryToBCD_Score_digit2), .Digit1(u_BinaryToBCD_Score_digit1),
    .Digit0(u_BinaryToBCD_Score_digit0), .CLR(u_BinaryToBCD_Score_clr), .EN(u_BinaryToBCD_Score_en));
  LED led_49 (.in(u_control_circuit_display5[11]));
  LED led_50 (.in(u_control_circuit_display4[11]));
  LED led_51 (.in(u_control_circuit_display3[11]));
  LED led_52 (.in(u_control_circuit_display2[11]));
  LED led_53 (.in(u_control_circuit_display1[11]));
  LED led_54 (.in(u_control_circuit_display0[11]));
  // RGBLED rgbled_9: pin names not known; wires that end beside it: u_control_circuit_ground_fig[11], u_control_circuit_ground[11], 1'b0
  Seven_Seg seven_seg_3 (
    .a(u_SegDecoder_3_seg[0]), .b(u_SegDecoder_3_seg[1]), .c(u_SegDecoder_3_seg[2]),
    .d(u_SegDecoder_3_seg[3]), .e(u_SegDecoder_3_seg[4]), .f(u_SegDecoder_3_seg[5]),
    .g(u_SegDecoder_3_seg[6]), .dp(1'b0));
  LED led_55 (.in(u_control_circuit_display5[10]));
  LED led_56 (.in(u_control_circuit_display4[10]));
  LED led_57 (.in(u_control_circuit_display3[10]));
  LED led_58 (.in(u_control_circuit_display2[10]));
  LED led_59 (.in(u_control_circuit_display1[10]));
  LED led_60 (.in(u_control_circuit_display0[10]));
  // RGBLED rgbled_10: pin names not known; wires that end beside it: u_control_circuit_ground_fig[10], u_control_circuit_ground[10], 1'b0
  LED led_61 (.in(u_control_circuit_display5[9]));
  LED led_62 (.in(u_control_circuit_display4[9]));
  LED led_63 (.in(u_control_circuit_display3[9]));
  LED led_64 (.in(u_control_circuit_display2[9]));
  LED led_65 (.in(u_control_circuit_display1[9]));
  LED led_66 (.in(u_control_circuit_display0[9]));
  // RGBLED rgbled_11: pin names not known; wires that end beside it: u_control_circuit_ground_fig[9], u_control_circuit_ground[9], 1'b0
  SegDecoder #(.applicationType("GHDL")) u_SegDecoder_4 (
    .Number(u_BinaryToBCD_Score_digit0), .up(1'b1), .Seg(u_SegDecoder_4_seg));  // open: down
  LED led_67 (.in(u_control_circuit_display5[8]));
  LED led_68 (.in(u_control_circuit_display4[8]));
  LED led_69 (.in(u_control_circuit_display3[8]));
  LED led_70 (.in(u_control_circuit_display2[8]));
  LED led_71 (.in(u_control_circuit_display1[8]));
  LED led_72 (.in(u_control_circuit_display0[8]));
  // RGBLED rgbled_12: pin names not known; wires that end beside it: u_control_circuit_ground_fig[8], u_control_circuit_ground[8], 1'b0
  Seven_Seg seven_seg_4 (
    .a(u_SegDecoder_4_seg[0]), .b(u_SegDecoder_4_seg[1]), .c(u_SegDecoder_4_seg[2]),
    .d(u_SegDecoder_4_seg[3]), .e(u_SegDecoder_4_seg[4]), .f(u_SegDecoder_4_seg[5]),
    .g(u_SegDecoder_4_seg[6]), .dp(1'b0));
  LED led_73 (.in(u_control_circuit_display5[7]));
  LED led_74 (.in(u_control_circuit_display4[7]));
  LED led_75 (.in(u_control_circuit_display3[7]));
  LED led_76 (.in(u_control_circuit_display2[7]));
  LED led_77 (.in(u_control_circuit_display1[7]));
  LED led_78 (.in(u_control_circuit_display0[7]));
  // RGBLED rgbled_13: pin names not known; wires that end beside it: u_control_circuit_ground_fig[7], u_control_circuit_ground[7], 1'b0
  LED led_79 (.in(u_control_circuit_display5[6]));
  LED led_80 (.in(u_control_circuit_display4[6]));
  LED led_81 (.in(u_control_circuit_display3[6]));
  LED led_82 (.in(u_control_circuit_display2[6]));
  LED led_83 (.in(u_control_circuit_display1[6]));
  LED led_84 (.in(u_control_circuit_display0[6]));
  // RGBLED rgbled_14: pin names not known; wires that end beside it: u_control_circuit_ground_fig[6], u_control_circuit_ground[6], 1'b0
  LED led_85 (.in(u_control_circuit_display5[5]));
  LED led_86 (.in(u_control_circuit_display4[5]));
  LED led_87 (.in(u_control_circuit_display3[5]));
  LED led_88 (.in(u_control_circuit_display2[5]));
  LED led_89 (.in(u_control_circuit_display1[5]));
  LED led_90 (.in(u_control_circuit_display0[5]));
  // RGBLED rgbled_15: pin names not known; wires that end beside it: u_control_circuit_ground_fig[5], u_control_circuit_ground[5], 1'b0
  LED led_91 (.in(u_control_circuit_display5[4]));
  LED led_92 (.in(u_control_circuit_display4[4]));
  LED led_93 (.in(u_control_circuit_display3[4]));
  LED led_94 (.in(u_control_circuit_display2[4]));
  LED led_95 (.in(u_control_circuit_display1[4]));
  LED led_96 (.in(u_control_circuit_display0[4]));
  // RGBLED rgbled_16: pin names not known; wires that end beside it: u_control_circuit_ground_fig[4], u_control_circuit_ground[4], 1'b0
  LED led_97 (.in(u_control_circuit_display5[3]));
  LED led_98 (.in(u_control_circuit_display4[3]));
  LED led_99 (.in(u_control_circuit_display3[3]));
  LED led_100 (.in(u_control_circuit_display2[3]));
  LED led_101 (.in(u_control_circuit_display1[3]));
  LED led_102 (.in(u_control_circuit_display0[3]));
  // RGBLED rgbled_17: pin names not known; wires that end beside it: u_control_circuit_ground_fig[3], u_control_circuit_ground[3], 1'b0
  LED led_103 (.in(u_control_circuit_display5[2]));
  LED led_104 (.in(u_control_circuit_display4[2]));
  LED led_105 (.in(u_control_circuit_display3[2]));
  LED led_106 (.in(u_control_circuit_display2[2]));
  LED led_107 (.in(u_control_circuit_display1[2]));
  LED led_108 (.in(u_control_circuit_display0[2]));
  // RGBLED rgbled_18: pin names not known; wires that end beside it: u_control_circuit_ground_fig[2], u_control_circuit_ground[2], 1'b0
  LED led_109 (.in(u_control_circuit_display5[1]));
  LED led_110 (.in(u_control_circuit_display4[1]));
  LED led_111 (.in(u_control_circuit_display3[1]));
  LED led_112 (.in(u_control_circuit_display2[1]));
  LED led_113 (.in(u_control_circuit_display1[1]));
  LED led_114 (.in(u_control_circuit_display0[1]));
  // RGBLED rgbled_19: pin names not known; wires that end beside it: u_control_circuit_ground_fig[1], u_control_circuit_ground[1], 1'b0
  LED led_115 (.in(u_control_circuit_display5[0]));
  LED led_116 (.in(u_control_circuit_display4[0]));
  LED led_117 (.in(u_control_circuit_display3[0]));
  LED led_118 (.in(u_control_circuit_display2[0]));
  LED led_119 (.in(u_control_circuit_display1[0]));
  LED led_120 (.in(u_control_circuit_display0[0]));
  // RGBLED rgbled_20: pin names not known; wires that end beside it: u_control_circuit_ground_fig[0], u_control_circuit_ground[0], 1'b0

  // Notes on the sheet:
  //   clk_2hz: Hz: 2
  //   clk_5hz: Hz: 5
  //   clk_10hz: Hz: 10
  //   clk: Hz: 3
  //   clk_2: Hz: 2
endmodule

/* Code of control_circuit:
library ieee;
use ieee.std_logic_1164.all;
use ieee.numeric_std.all;

entity control_circuit is	
	port	(
		-- Input ports
		clk_1hz, clk_2hz, clk_5hz, clk_10hz : in std_logic;
		start, replay, jump, squat : in std_logic;
		rand2, rand0 : in std_logic;	
		block_temp : in std_logic_vector(5 downto 0);
		-- Output ports
		time_signal : out std_logic_vector(5 downto 0);	
		q_signal : out std_logic_vector(5 downto 0);	
		ground : out std_logic_vector(19 downto 0);
		ground_fig : out std_logic_vector(19 downto 0);
		display5, display4, display3, display2, display1, display0 : out std_logic_vector(19 downto 0);	
		player_display : out std_logic_vector(5 downto 0));
end control_circuit;

architecture control of control_circuit is	
	signal Q : integer := 0;
	signal Start_signal : integer := 0;
	signal Time : integer := 0; --遊戲執行的時間
	signal StartTime: integer:= 0; --遊戲開始後動畫停滯時間用--
	signal GameOverTime: integer:=0; --遊戲結束後動畫停滯時間用--
	signal Level : integer := 0;
	signal ground_signal: std_logic_vector(19 downto 0) := "00000000000000000000";
------------player signal-----------------------------------------------------
	signal pattern_jump : std_logic_vector(5 downto 0) := "011100";
	signal pattern_squat: std_logic_vector(5 downto 0) := "000001";
	signal pattern_start: std_logic_vector(5 downto 0) := "000111";
	signal pattern_reset: std_logic_vector(5 downto 0) := "000000";
------------block signal------------------------------------------------------
	signal block_2: std_logic_vector(19 downto 0) := "00000000000000000000";
	signal block_0: std_logic_vector(19 downto 0) := "00000000000000000000";
	signal block_zero: std_logic_vector(19 downto 0) := "00000000000000000000";
	signal crush : std_logic := '0';
------------game over display-------------------------------------------------
	signal gg6: std_logic_vector(19 downto 0) := "00001111000001111000";
	signal gg5: std_logic_vector(19 downto 0) := "00011001100011001100";
	signal gg4: std_logic_vector(19 downto 0) := "00011000000011000000";
	signal gg3: std_logic_vector(19 downto 0) := "00011000000011000000";
	signal gg2: std_logic_vector(19 downto 0) := "00011011100011011100";
	signal gg1: std_logic_vector(19 downto 0) := "00011001100011001100";
	signal gg0: std_logic_vector(19 downto 0) := "00001111000001111000";
------------open display 1-------------------------------------------------
	signal first6: std_logic_vector(19 downto 0) := "00000000011000000000";
	signal first5: std_logic_vector(19 downto 0) := "00000000101000000000";
	signal first4: std_logic_vector(19 downto 0) := "00000000001000000000";
	signal first3: std_logic_vector(19 downto 0) := "00000000001000000000";
	signal first2: std_logic_vector(19 downto 0) := "00000000001000000000";
	signal first1: std_logic_vector(19 downto 0) := "00000000001000000000";
	signal first0: std_logic_vector(19 downto 0) := "00000000111100000000";
------------open display 2-------------------------------------------------
	signal second6: std_logic_vector(19 downto 0) := "00000000011000000000";
	signal second5: std_logic_vector(19 downto 0) := "00000000100100000000";
	signal second4: std_logic_vector(19 downto 0) := "00000000000100000000";
	signal second3: std_logic_vector(19 downto 0) := "00000000000100000000";
	signal second2: std_logic_vector(19 downto 0) := "00000000001000000000";
	signal second1: std_logic_vector(19 downto 0) := "00000000010000000000";
	signal second0: std_logic_vector(19 downto 0) := "00000000111100000000";
------------open display 3--------------------------------------------------
	signal third6: std_logic_vector(19 downto 0) := "00000000011100000000";
	signal third5: std_logic_vector(19 downto 0) := "00000000100010000000";
	signal third4: std_logic_vector(19 downto 0) := "00000000000100000000";
	signal third3: std_logic_vector(19 downto 0) := "00000000001000000000";
	signal third2: std_logic_vector(19 downto 0) := "00000000000100000000";
	signal third1: std_logic_vector(19 downto 0) := "00000000100010000000";
	signal third0: std_logic_vector(19 downto 0) := "00000000011100000000";
------------------------------------------------------------------------------
Begin
------------------display-----------------------------------------------------
display5 <= gg6 when  Q = 6
		else third6 when StartTime = 1
		else second6 when StartTime = 2
		else first6 when StartTime = 3
		else block_zero;
display4 <= gg5 when  Q = 6
		else third5 when StartTime = 1
		else second5 when StartTime = 2
		else first5 when StartTime = 3
		else block_zero;
display3 <= gg4 when  Q = 6
		else third4 when StartTime = 1
		else second4 when StartTime = 2
		else first4 when StartTime = 3
		else block_zero;
display2 <= gg3 when  Q = 6
		else third3 when StartTime = 1
		else second3 when StartTime = 2
		else first3 when StartTime = 3
		else block_2;
display1 <= gg2 when  Q = 6
		else third2 when StartTime = 1
		else second2 when StartTime = 2
		else first2 when StartTime = 3
		else block_zero;
display0 <= gg1 when  Q = 6
		else third1 when StartTime = 1
		else second1 when StartTime = 2
		else first1 when StartTime = 3
		else block_0;
ground <= ground_signal when (Q = 2 or Q = 3 or Q = 4 or Q = 5)
		else "00000000000000000000";
ground_fig <= gg0 when  Q = 6
		else third0 when StartTime = 1
		else second0 when StartTime = 2
		else first0 when StartTime = 3
		else "00000000000000000000";

time_signal <= std_logic_vector(to_unsigned(time, 6));
q_signal <= std_logic_vector(to_unsigned(q, 6));
----------------player figures------------------------------------------------
	player_display <= pattern_jump when  (jump = '1') and (Q = 2 or Q = 3 or Q = 4 or Q = 5)
		else pattern_squat when (squat = '1') and (Q = 2 or  Q = 3 or Q = 4 or Q = 5)
		else pattern_start when (squat = '0') and (jump = '0') and (Q = 2 or Q = 3 or Q = 4 or Q = 5)
		else pattern_reset;
----------------crush signal-------------------------------------------------
	crush <= (player_display(0) and block_temp(0))
		or (player_display(1) and block_temp(1))
		or (player_display(2) and block_temp(2))
		or (player_display(3) and block_temp(3))
		or (player_display(4) and block_temp(4))
		or (player_display(5) and block_temp(5));
------------------state control------------------------------------------------
process(clk_1hz, clk_2hz, clk_5hz, clk_10hz, Q, start) is
 	begin
		if (Q = 0) and (start = '1' or replay = '1') then
			Q <= 1;
		end if;

		if (Q = 1) then --開機畫面待做
			if (rising_edge(clk_1hz)) then 
				StartTime <= StartTime + 1;
			end if;
			if(StartTime = 4) then  
				Q <= 2; StartTime <= 0; 
			end if;
		end if;

		if (Q = 2) then --level1
			ground_signal <= "11111111111111111111";
			if (rising_edge(clk_1hz)) then 
				Time <= Time + 1;
			end if;
			if(Time = 25) then  
				Q <= 3; Time <= 0; 
			end if;
			if(crush = '1') then  
				Q <= 6; Time <= 0; 
			end if;
		end if;

		if (Q = 3) then  --level2
			ground_signal <= "11111111111111111111";
			if (rising_edge(clk_1hz)) then 
				Time <= Time + 1;
			end if;
			if(Time = 40) then  
				Q <= 4; Time <= 0; 
			end if;
			if(crush = '1') then  
				Q <= 6; Time <= 0; 
			end if;
		end if;

		if (Q = 4) then  --level3
			ground_signal <= "11111111111111111111";
			if (rising_edge(clk_1hz)) then 
				Time <= Time + 1;
			end if;
			if(Time = 60) then  
				Q <= 5; Time <= 0; 
			end if;
			if(crush = '1') then  
				Q <= 6; Time <= 0; 
			end if;
		end if;

		if (Q = 5) then  --level4
			ground_signal <= "11111111111111111111";
			if(crush = '1') then  
				Q <= 6; 
			end if;
		end if;

		if (Q = 6) then --遊戲結束
			if (rising_edge(clk_1hz)) then 
				GameOverTime <= GameOverTime + 1;
			end if;
			if(GameOverTime > 2) and (GameOverTime < 7) then  --gg待做
				block_2 <= "00000000000000000000" ;
				block_0 <= "00000000000000000000" ;
				ground_signal <= "00000000000000000000";
			end if;
			if (GameOverTime > 7) then  
				Q <= 0; GameOverTime <= 0; Start_signal <= 0; 
			end if;
		end if;
----------------block generator level1----------------------------------------
		if (rising_edge(clk_1hz)) and (Q = 2) then
			if (block_2(0) and rand2) or (block_0(0) and rand2)then
				block_2 <= block_2(18 downto 0) & "0";
			else block_2 <= block_2(18 downto 0) & rand2;
			end if;
			if (block_0(0) and rand0) or (block_2(0) and rand0) then
				block_0 <= block_0(18 downto 0) & "0";
			else block_0 <= block_0(18 downto 0) & rand0;
			end if;
		end if;
----------------block generator level2----------------------------------------
		if (rising_edge(clk_2hz)) and (Q = 3) then
			if (block_2(0) and rand2) or (block_0(0) and rand2)then
				block_2 <= block_2(18 downto 0) & "0";
			else block_2 <= block_2(18 downto 0) & rand2;
			end if;
			if (block_0(0) and rand0) or (block_2(0) and rand0) then
				block_0 <= block_0(18 downto 0) & "0";
			else block_0 <= block_0(18 downto 0) & rand0;
			end if;
		end if;
----------------block generator level3----------------------------------------
		if (rising_edge(clk_5hz)) and (Q = 4) then
			if (block_2(0) and rand2) or (block_0(0) and rand2)then
				block_2 <= block_2(18 downto 0) & "0";
			else block_2 <= block_2(18 downto 0) & rand2;
			end if;
			if (block_0(0) and rand0) or (block_2(0) and rand0) then
				block_0 <= block_0(18 downto 0) & "0";
			else block_0 <= block_0(18 downto 0) & rand0;
			end if;
		end if;
----------------block generator level4----------------------------------------
		if (rising_edge(clk_2hz)) and (Q = 5) then
			if (block_2(0) and rand2) or (block_0(0) and rand2)then
				block_2 <= block_2(18 downto 0) & "0";
			else block_2 <= block_2(18 downto 0) & rand2;
			end if;
			if (block_0(0) and rand0) or (block_2(0) and rand0) then
				block_0 <= block_0(18 downto 0) & "0";
			else block_0 <= block_0(18 downto 0) & rand0;
			end if;
		end if;
--------------------------------------------------------------------------------
end process;
end control;
*/

/* Code of SCORE:
LIBRARY ieee;
USE ieee.std_logic_1164.all;
USE ieee.numeric_std.all;


entity SCORE is
port (
On_Off: in std_logic;
S,C,O,R,E: out std_logic_vector(15 downto 0));
end SCORE;


architecture Behaviors of SCORE is

begin

S <= "0000001110111011" when On_Off = '1'
else "0000000000000000";
C <= "0000000011110011" when On_Off = '1'
else "0000000000000000";
O <= "0000000011111111" when On_Off = '1'
else "0000000000000000";
R <= "0010001111000111" when On_Off = '1'
else "0000000000000000";
E <= "0000001111110011" when On_Off = '1'
else "0000000000000000";

end Behaviors;
*/

/* Code of LEVEL:
LIBRARY ieee;
USE ieee.std_logic_1164.all;
USE ieee.numeric_std.all;


entity LEVEL is
port (
On_Off: in std_logic;
L,E,V: out std_logic_vector(15 downto 0));
end LEVEL;


architecture Behaviors of LEVEL is

begin

L <= "0000000011110000" when On_Off = '1'
else "0000000000000000";
E <= "0000001111110011" when On_Off = '1'
else "0000000000000000";
V <= "1001000011000000" when On_Off = '1'
else "0000000000000000";

end Behaviors;
*/

/* Code of SegDecoder:
LIBRARY ieee;
USE ieee.std_logic_1164.all;
USE ieee.numeric_std.all;


entity SegDecoder is
port (
Number: in std_logic_vector(3 downto 0);
up: in std_logic;
Seg: out std_logic_vector(6 downto 0);
down: out std_logic);
end SegDecoder;


architecture Behaviors of SegDecoder is
signal upNumber : std_logic_vector(4 downto 0);
begin
upNumber <= up&Number;
Seg <= "1101111" when Number = "1001"
else "1111111" when Number = "1000"
else "0000111" when Number = "0111"
else "1111101" when Number = "0110"
else "1101101" when Number = "0101"
else "1100110" when Number = "0100"
else "1001111" when Number = "0011"
else "1011011" when Number = "0010"
else "0000110" when Number = "0001"
else "0000000" when upNumber = "00000"
else "0111111" when upNumber = "10000";

down <= '0' when upNumber = "00000"
else '1';

end Behaviors;
*/

/* Code of Q:
LIBRARY ieee;
USE ieee.std_logic_1164.all;
USE ieee.numeric_std.all;


entity Q is
port (
On_Off,clk: in std_logic;
q_signal:in std_logic_vector(5 downto 0);
qq: out std_logic_vector(0 to 15));
end Q;


architecture Behaviors of Q is
begin
qq <= "0000000011111111" when q_signal = "000001" else
      "0000000000001100" when q_signal = "000010" else
      "0000001101110111" when q_signal = "000011" else
      "0000001100111111" when q_signal = "000100" else
      "0000001110001100" when q_signal = "000101";

end Behaviors;
*/

/* Code of BinaryToBCD_Score:
LIBRARY ieee;
USE ieee.std_logic_1164.all;
USE ieee.numeric_std.all;

entity BinaryToBCD_Score is
port (
Score: in std_logic_vector(19 downto 0);
qq: in std_logic_vector(5 downto 0);
Digit3,Digit2,Digit1,Digit0: out std_logic_vector(3 downto 0);
CLR, EN: out std_logic);
end BinaryToBCD_Score;

architecture Behaviors of BinaryToBCD_Score is

signal Score_int : integer := 0;
signal q :std_logic_vector(5 downto 0);

begin
q <= qq;
with q select
CLR <= '1' when "000001",
	'0' when others;
with q select
EN <= '0' when "000000",
	'0' when "000001",
	'0' when "000110",
	'1' when others;
Score_int <= to_integer(unsigned(Score));
Digit3 <= std_logic_vector(to_unsigned((Score_int/1000)REM 10,4));
Digit2 <= std_logic_vector(to_unsigned((Score_int/100)REM 10,4));
Digit1 <= std_logic_vector(to_unsigned((Score_int/10)REM 10,4));
Digit0 <= std_logic_vector(to_unsigned(Score_int REM 10,4));
end Behaviors;
*/
