// Digital circuit random.dig as structural Verilog
module random (
  input  clk,
  input  start,
  input  [1:0] seed,
  input  stop,
  output [1:0] \rand 
);

  wire prng_1_r, prng_2_r;

  PRNG prng_1 (.S(seed[0]), .se(stop), .ne(start), .C(clk), .R(prng_1_r));
  PRNG prng_2 (.S(seed[1]), .se(stop), .ne(start), .C(clk), .R(prng_2_r));
  random #(.applicationType("GHDL")) u_random (.clk(clk), .a(prng_1_r), .b(prng_2_r), .\rand (\rand ));
endmodule

/* Code of random:
library ieee;
use ieee.std_logic_1164.all;
use ieee.numeric_std.all;

entity random is	
	port(
		-- Input ports
		clk, a, b : in std_logic;
		-- Output ports		
		rand: out std_logic_vector(1 downto 0));
end random;

architecture random of random is	
Begin
	process(clk) is
 	begin
 		if(rising_edge(clk)) then
			--輸出
			if (a and b) then rand <= "00";
			elsif a  then rand <= "01";
			elsif b  then rand <= "10";
			else rand <= "00";
			end if;
		end if;
	end process; 
end random;
*/
