// Digital circuit rotationLED.dig as structural Verilog
module rotationLED (
  input  gameover,
  input  rotation_speed,
  input  clk,
  output row3,
  output row1
);

  wire [19:0] u_led_rotation_ledout_0, u_led_rotation_ledout_1;

  random_0_1 #(.applicationType("GHDL")) u_random_0_1 (.clk(clk), .\output (row3));
  led_rotation #(.applicationType("GHDL")) u_led_rotation (
    .Reset(gameover), .clk(rotation_speed), .random0(row3), .random1(row1),
    .LEDout_0(u_led_rotation_ledout_0), .LEDout_1(u_led_rotation_ledout_1));
  random_0_1 #(.applicationType("GHDL")) u_random_0_1_2 (.clk(clk), .\output (row1));
  LED led_1 (.in(u_led_rotation_ledout_0[19]));
  LED led_2 (.in(u_led_rotation_ledout_0[18]));
  LED led_3 (.in(u_led_rotation_ledout_1[19]));
  LED led_4 (.in(u_led_rotation_ledout_1[18]));
  LED led_5 (.in(u_led_rotation_ledout_0[17]));
  LED led_6 (.in(u_led_rotation_ledout_0[16]));
  LED led_7 (.in(u_led_rotation_ledout_1[17]));
  LED led_8 (.in(u_led_rotation_ledout_1[16]));
  LED led_9 (.in(u_led_rotation_ledout_0[15]));
  LED led_10 (.in(u_led_rotation_ledout_0[14]));
  LED led_11 (.in(u_led_rotation_ledout_1[15]));
  LED led_12 (.in(u_led_rotation_ledout_1[14]));
  LED led_13 (.in(u_led_rotation_ledout_0[13]));
  LED led_14 (.in(u_led_rotation_ledout_0[12]));
  LED led_15 (.in(u_led_rotation_ledout_1[13]));
  LED led_16 (.in(u_led_rotation_ledout_1[12]));
  LED led_17 (.in(u_led_rotation_ledout_0[11]));
  LED led_18 (.in(u_led_rotation_ledout_0[10]));
  LED led_19 (.in(u_led_rotation_ledout_1[11]));
  LED led_20 (.in(u_led_rotation_ledout_1[10]));
  LED led_21 (.in(u_led_rotation_ledout_0[8]));
  LED led_22 (.in(u_led_rotation_ledout_0[9]));
  LED led_23 (.in(u_led_rotation_ledout_1[8]));
  LED led_24 (.in(u_led_rotation_ledout_1[9]));
  LED led_25 (.in(u_led_rotation_ledout_0[7]));
  LED led_26 (.in(u_led_rotation_ledout_0[6]));
  LED led_27 (.in(u_led_rotation_ledout_1[7]));
  LED led_28 (.in(u_led_rotation_ledout_1[6]));
  LED led_29 (.in(u_led_rotation_ledout_0[4]));
  LED led_30 (.in(u_led_rotation_ledout_0[5]));
  LED led_31 (.in(u_led_rotation_ledout_1[4]));
  LED led_32 (.in(u_led_rotation_ledout_1[5]));
  LED led_33 (.in(u_led_rotation_ledout_0[3]));
  LED led_34 (.in(u_led_rotation_ledout_0[2]));
  LED led_35 (.in(u_led_rotation_ledout_1[3]));
  LED led_36 (.in(u_led_rotation_ledout_1[2]));
  LED led_37 (.in(u_led_rotation_ledout_0[0]));
  LED led_38 (.in(u_led_rotation_ledout_0[1]));
  LED led_39 (.in(u_led_rotation_ledout_1[0]));
  LED led_40 (.in(u_led_rotation_ledout_1[1]));

  // Notes on the sheet:
  //   rotation_speed: Hz: 5
  //   clk: Hz: 2
endmodule

/* Code of random_0_1:
library ieee;
use ieee.std_logic_1164.all;
use ieee.numeric_std.all;

entity random_0_1 is	
	port(
		-- Input ports
		clk : in std_logic;
		-- Output ports		
		output : out std_logic);
end random_0_1;

architecture random of random_0_1 is	
	signal z : integer:= 0 ;
Begin
	process(clk) is
 	begin
 		if(rising_edge(clk)) then
			if(z = 0) then z <= 1;
			elsif(z = 1) then z <= 2;
			elsif(z = 2) then z <= 3;
			elsif(z = 3) then z <= 4;
			elsif(z = 4) then z <= 5;
			elsif(z = 5) then z <= 6;
			elsif(z = 6) then z <= 7;
			elsif(z = 7) then z <= 8;
			elsif(z = 8) then z <= 9;
			elsif(z = 9) then z <= 10;
			elsif(z = 10) then z <= 11;
			elsif(z = 11) then z <= 12;
			elsif(z = 12) then z <= 13;
			elsif(z = 13) then z <= 14;
			elsif(z = 14) then z <= 15;
			elsif(z = 15) then z <= 16;
			elsif(z = 16) then z <= 17;
			elsif(z = 17) then z <= 18;
			elsif(z = 18) then z <= 19;
			elsif(z = 19) then z <= 20;
			elsif(z = 20) then z <= 0;
			else z <= 0;
			end if;
			--輸出
			if(z = 4)  or (z = 10) or (z = 16)  then output <= '1';
			else output <= '0';
			end if;
		end if;
	end process; 
end random;
*/

/* Code of led_rotation:
library ieee;
use ieee.std_logic_1164.all;
use ieee.numeric_std.all;

entity led_rotation is	
	port	(
		-- Input ports
		Reset, clk, random0, random1 : in  std_logic;
		-- Output ports
		LEDout_0, LEDout_1 : out std_logic_vector(19 downto 0));
end led_rotation;

architecture rotation of led_rotation is	
	signal pattern_0 : std_logic_vector(19 downto 0) := "00000000000000000000";	
	signal pattern_1 : std_logic_vector(19 downto 0) := "00000000000000000000";	
	signal rand0, rand1 : std_logic;
begin
--------LED rotation-------------------------------------------------------------
	LEDout_0 <= pattern_0;
	LEDout_1 <= pattern_1;
	rand0 <= '0' when  (random0 = '1') and (random1 = '1')
		else random0;
	rand1 <= '0' when  (random0 = '1') and (random1 = '1')
		else random1;

	process(CLK, RESET)
	begin
		if RESET = '1' then
			pattern_0 <= "00000000000000000000";
			pattern_1 <= "00000000000000000000";
		elsif rising_edge(CLK) then
			pattern_0 <= pattern_0(18 downto 0) & rand0;
			pattern_1 <= pattern_1(18 downto 0) & rand1;
		end if;
-----------------------------------------------------------------------------
	end process;
end rotation;
*/

/* Code of random_0_1:
library ieee;
use ieee.std_logic_1164.all;
use ieee.numeric_std.all;

entity random_0_1 is	
	port(
		-- Input ports
		clk : in std_logic;
		-- Output ports		
		output : out std_logic);
end random_0_1;

architecture random of random_0_1 is	
	signal z : integer:= 0 ;
Begin
	process(clk) is
 	begin
 		if(rising_edge(clk)) then
			if(z = 0) then z <= 1;
			elsif(z = 1) then z <= 2;
			elsif(z = 2) then z <= 3;
			elsif(z = 3) then z <= 4;
			elsif(z = 4) then z <= 5;
			elsif(z = 5) then z <= 6;
			elsif(z = 6) then z <= 7;
			elsif(z = 7) then z <= 8;
			elsif(z = 8) then z <= 9;
			elsif(z = 9) then z <= 10;
			elsif(z = 10) then z <= 11;
			elsif(z = 11) then z <= 12;
			elsif(z = 12) then z <= 13;
			elsif(z = 13) then z <= 14;
			elsif(z = 14) then z <= 15;
			elsif(z = 15) then z <= 16;
			elsif(z = 16) then z <= 17;
			elsif(z = 17) then z <= 18;
			elsif(z = 18) then z <= 19;
			elsif(z = 19) then z <= 20;
			elsif(z = 20) then z <= 0;
			else z <= 0;
			end if;
			--輸出
			if(z = 0) or (z = 7) or (z = 13) then output <= '1';
			else output <= '0';
			end if;
		end if;
	end process; 
end random;
*/
