// Digital circuit test.dig as structural Verilog
module test (
  input  start,
  input  reset
);

  wire DOWN_out, UP_out;
  wire [3:0] u_control_circuit_col_display;
  wire [5:0] u_control_circuit_row_display;

  Button UP (.out(UP_out));
  Button DOWN (.out(DOWN_out));
  control_circuit #(.applicationType("GHDL")) u_control_circuit (
    .clk(start), .start(UP_out), .jump(DOWN_out), .squat(reset), .row_display(u_control_circuit_row_display),
    .col_display(u_control_circuit_col_display));  // open: reset, random
  LedMatrix #(.colAddrBits(4), .rowDataBits(6)) ledmatrix_1 (
    .rows(u_control_circuit_row_display), .column(u_control_circuit_col_display));
endmodule

/* Code of control_circuit:
library ieee;
use ieee.std_logic_1164.all;

entity control_circuit is	
	port	(
		-- Input ports
		clk, start, jump, squat,reset: in std_logic;
		random : in std_logic_vector(1 downto 0);	
		-- Output ports
		row_display : out std_logic_vector(5 downto 0);	
		col_display : out std_logic_vector(3 downto 0));
end control_circuit;

architecture state_graph of control_circuit is	
	signal out_vector : std_logic_vector(3 downto 0) := "0000";
	signal state : std_logic_vector(2 downto 0):= "000";

------------player signal-----------------------------------------------------
	signal pattern_jump : std_logic_vector(5 downto 0) := "001110";
	signal pattern_squat: std_logic_vector(5 downto 0) := "100000";
	signal pattern_start: std_logic_vector(5 downto 0) := "111000";
	signal pattern_reset: std_logic_vector(5 downto 0) := "000000";
	signal player_row: std_logic_vector(5 downto 0) ;
	signal player_col: std_logic := '0';
------------block signal------------------------------------------------------
	signal low_block: std_logic_vector(5 downto 0) := "100000";
	signal high_block: std_logic_vector(5 downto 0) := "001000";
	signal no_block: std_logic_vector(5 downto 0) := "000000";
	signal block_temp: std_logic_vector(5 downto 0) ;
	signal block_row: std_logic_vector(5 downto 0) ;
	signal block_col: std_logic_vector(3 downto 0) ;
	signal rand_num : integer := 0 ;
	
------------------------------------------------------------------------------
Begin
------------------display-----------------------------------------------------
row_display(0) <= player_row(0); --or block(0);
row_display(1) <= player_row(1); --or block(1);
row_display(2) <= player_row(2); --or block(2);
row_display(3) <= player_row(3); --or block(3);
row_display(4) <= player_row(4); --or block(4);
row_display(5) <= player_row(5); --or block(5);

col_display(0) <= '0'; --or block(0);
col_display(1) <= player_col; --or block(0);
col_display(2) <= '0'; --or block(0);
col_display(3) <= '0'; --or block(0);
----------------player figure-------------------------------------------------
	player_row <= pattern_jump when  (jump = '1') and (start = '1')
		else pattern_squat when (squat = '1') and (start = '1')
		else pattern_start when (squat = '0') and (jump = '0') and (start = '1')
		else pattern_reset;
	player_col <= '1' when  (start = '1')
		else '0';
----------------block generator-----------------------------------------------
	rand_num <= to_integer(unsigened(num));	
	block_temp <= low_block when  (rand_num = 0) and (start = '1')
		else high_block when (rand_num = 1) and (start = '1')
		else no_block when (rand_num = 2) and (start = '1')
		else no_block;

	process(clk)
	begin
		if over = '1' then
			pattern_0 <= "00000000000000000000";
			pattern_1 <= "00000000000000000000";
		elsif rising_edge(CLK) then
			pattern_0 <= pattern_0(18 downto 0) & rand0;
			pattern_1 <= pattern_1(18 downto 0) & rand1;
		end if;

		if(block_col = "0000") then block_col <= "0001";
		elsif(block_col = "0001") then  block_col <= "0010"; block_row <= block_temp;
		elsif(block_col = "0010") then  block_col <= "0010";
		elsif(block_col = "0011") then  block_col <= "0010";
		elsif(block_col = "0100") then  block_col <= "0010";
		elsif(block_col = "0101") then  block_col <= "0010";
		elsif(block_col = "0110") then  block_col <= "0010";
		elsif(block_col = "0111") then  block_col <= "0010";
		elsif(block_col = "1000") then  block_col <= "0010";
		elsif(block_col = "1001") then  block_col <= "0010";
		elsif(block_col = "1010") then  block_col <= "0010";
		elsif(block_col = "1011") then  block_col <= "0010";
		elsif(block_col = "1100") then  block_col <= "0010";
		elsif(block_col = "1101") then  block_col <= "0010";
		elsif(block_col = "1110") then  block_col <= "0010";		elsif(block_col = "0011") then  block_col <= "0010";
		elsif(block_col = "1111") then  block_col <= "0010";
		end if;



end state_graph;
*/
