// Digital circuit test_block.dig as structural Verilog
module test_block (
  input  clk_2hz,
  input  in_2,
  input  [1:0] seed,
  input  clk_1hz,
  input  clk_5hz,
  input  clk_10hz,
  input  start,
  input  replay,
  output [1:0] out_9,
  output [5:0] out_10,
  output [5:0] out_11
);

  wire DOWN_out, or_1_out, or_2_out, or_3_out, or_4_out, or_5_out, or_6_out, UP_out;
  wire [5:0] u_control_circuit_player_display;
  wire [19:0] u_control_circuit_display0, u_control_circuit_display1, u_control_circuit_display2,
       u_control_circuit_display3, u_control_circuit_display4, u_control_circuit_display5,
       u_control_circuit_ground;

  Button UP (.out(UP_out));
  Button DOWN (.out(DOWN_out));
  random random_1 (.clk(clk_1hz), .start(start), .seed(seed), .stop(in_2), .\rand (out_9));
  control_circuit #(.applicationType("GHDL")) u_control_circuit (
    .clk_1hz(clk_1hz), .clk_2hz(clk_2hz), .clk_5hz(clk_5hz), .clk_10hz(clk_10hz), .start(start),
    .jump(UP_out), .squat(DOWN_out), .replay(replay), .rand2(out_9[0]), .rand0(out_9[1]),
    .block_temp({u_control_circuit_display5[17], u_control_circuit_display4[17], u_control_circuit_display3[17], u_control_circuit_display2[17], u_control_circuit_display1[17], u_control_circuit_display0[17]}),
    .time_signal(out_11), .q_signal(out_10), .ground(u_control_circuit_ground),
    .display5(u_control_circuit_display5), .display4(u_control_circuit_display4),
    .display3(u_control_circuit_display3), .display2(u_control_circuit_display2),
    .display1(u_control_circuit_display1), .display0(u_control_circuit_display0),
    .player_display(u_control_circuit_player_display));
  or or_1 (or_1_out, u_control_circuit_display5[17], u_control_circuit_player_display[5]);
  or or_2 (or_2_out, u_control_circuit_display4[17], u_control_circuit_player_display[4]);
  or or_3 (or_3_out, u_control_circuit_display3[17], u_control_circuit_player_display[3]);
  or or_4 (or_4_out, u_control_circuit_display2[17], u_control_circuit_player_display[2]);
  or or_5 (or_5_out, u_control_circuit_display1[17], u_control_circuit_player_display[1]);
  or or_6 (or_6_out, u_control_circuit_display0[17], u_control_circuit_player_display[0]);
  LED led_1 (.in(u_control_circuit_display5[19]));
  LED led_2 (.in(u_control_circuit_display4[19]));
  LED led_3 (.in(u_control_circuit_display3[19]));
  LED led_4 (.in(u_control_circuit_display2[19]));
  LED led_5 (.in(u_control_circuit_display1[19]));
  LED led_6 (.in(u_control_circuit_display0[19]));
  LED led_7 (.in(u_control_circuit_ground[19]));
  LED led_8 (.in(u_control_circuit_display5[18]));
  LED led_9 (.in(u_control_circuit_display4[18]));
  LED led_10 (.in(u_control_circuit_display3[18]));
  LED led_11 (.in(u_control_circuit_display2[18]));
  LED led_12 (.in(u_control_circuit_display1[18]));
  LED led_13 (.in(u_control_circuit_display0[18]));
  LED led_14 (.in(u_control_circuit_ground[18]));
  LED led_15 (.in(or_1_out));
  LED led_16 (.in(or_2_out));
  LED led_17 (.in(or_3_out));
  LED led_18 (.in(or_4_out));
  LED led_19 (.in(or_5_out));
  LED led_20 (.in(or_6_out));
  LED led_21 (.in(u_control_circuit_ground[17]));
  LED led_22 (.in(u_control_circuit_display5[16]));
  LED led_23 (.in(u_control_circuit_display4[16]));
  LED led_24 (.in(u_control_circuit_display3[16]));
  LED led_25 (.in(u_control_circuit_display2[16]));
  LED led_26 (.in(u_control_circuit_display1[16]));
  LED led_27 (.in(u_control_circuit_display0[16]));
  LED led_28 (.in(u_control_circuit_ground[16]));
  LED led_29 (.in(u_control_circuit_display5[15]));
  LED led_30 (.in(u_control_circuit_display4[15]));
  LED led_31 (.in(u_control_circuit_display3[15]));
  LED led_32 (.in(u_control_circuit_display2[15]));
  LED led_33 (.in(u_control_circuit_display1[15]));
  LED led_34 (.in(u_control_circuit_display0[15]));
  LED led_35 (.in(u_control_circuit_ground[15]));
  LED led_36 (.in(u_control_circuit_display5[14]));
  LED led_37 (.in(u_control_circuit_display4[14]));
  LED led_38 (.in(u_control_circuit_display3[14]));
  LED led_39 (.in(u_control_circuit_display2[14]));
  LED led_40 (.in(u_control_circuit_display1[14]));
  LED led_41 (.in(u_control_circuit_display0[14]));
  LED led_42 (.in(u_control_circuit_ground[14]));
  LED led_43 (.in(u_control_circuit_display5[13]));
  LED led_44 (.in(u_control_circuit_display4[13]));
  LED led_45 (.in(u_control_circuit_display3[13]));
  LED led_46 (.in(u_control_circuit_display2[13]));
  LED led_47 (.in(u_control_circuit_display1[13]));
  LED led_48 (.in(u_control_circuit_display0[13]));
  LED led_49 (.in(u_control_circuit_ground[13]));
  LED led_50 (.in(u_control_circuit_display5[12]));
  LED led_51 (.in(u_control_circuit_display4[12]));
  LED led_52 (.in(u_control_circuit_display3[12]));
  LED led_53 (.in(u_control_circuit_display2[12]));
  LED led_54 (.in(u_control_circuit_display1[12]));
  LED led_55 (.in(u_control_circuit_display0[12]));
  LED led_56 (.in(u_control_circuit_ground[12]));
  LED led_57 (.in(u_control_circuit_display5[11]));
  LED led_58 (.in(u_control_circuit_display4[11]));
  LED led_59 (.in(u_control_circuit_display3[11]));
  LED led_60 (.in(u_control_circuit_display2[11]));
  LED led_61 (.in(u_control_circuit_display1[11]));
  LED led_62 (.in(u_control_circuit_display0[11]));
  LED led_63 (.in(u_control_circuit_ground[11]));
  LED led_64 (.in(u_control_circuit_display5[10]));
  LED led_65 (.in(u_control_circuit_display4[10]));
  LED led_66 (.in(u_control_circuit_display3[10]));
  LED led_67 (.in(u_control_circuit_display2[10]));
  LED led_68 (.in(u_control_circuit_display1[10]));
  LED led_69 (.in(u_control_circuit_display0[10]));
  LED led_70 (.in(u_control_circuit_ground[10]));
  LED led_71 (.in(u_control_circuit_display5[9]));
  LED led_72 (.in(u_control_circuit_display4[9]));
  LED led_73 (.in(u_control_circuit_display3[9]));
  LED led_74 (.in(u_control_circuit_display2[9]));
  LED led_75 (.in(u_control_circuit_display1[9]));
  LED led_76 (.in(u_control_circuit_display0[9]));
  LED led_77 (.in(u_control_circuit_ground[9]));
  LED led_78 (.in(u_control_circuit_display5[8]));
  LED led_79 (.in(u_control_circuit_display4[8]));
  LED led_80 (.in(u_control_circuit_display3[8]));
  LED led_81 (.in(u_control_circuit_display2[8]));
  LED led_82 (.in(u_control_circuit_display1[8]));
  LED led_83 (.in(u_control_circuit_display0[8]));
  LED led_84 (.in(u_control_circuit_ground[8]));
  LED led_85 (.in(u_control_circuit_display5[7]));
  LED led_86 (.in(u_control_circuit_display4[7]));
  LED led_87 (.in(u_control_circuit_display3[7]));
  LED led_88 (.in(u_control_circuit_display2[7]));
  LED led_89 (.in(u_control_circuit_display1[7]));
  LED led_90 (.in(u_control_circuit_display0[7]));
  LED led_91 (.in(u_control_circuit_ground[7]));
  LED led_92 (.in(u_control_circuit_display5[6]));
  LED led_93 (.in(u_control_circuit_display4[6]));
  LED led_94 (.in(u_control_circuit_display3[6]));
  LED led_95 (.in(u_control_circuit_display2[6]));
  LED led_96 (.in(u_control_circuit_display1[6]));
  LED led_97 (.in(u_control_circuit_display0[6]));
  LED led_98 (.in(u_control_circuit_ground[6]));
  LED led_99 (.in(u_control_circuit_display5[5]));
  LED led_100 (.in(u_control_circuit_display4[5]));
  LED led_101 (.in(u_control_circuit_display3[5]));
  LED led_102 (.in(u_control_circuit_display2[5]));
  LED led_103 (.in(u_control_circuit_display1[5]));
  LED led_104 (.in(u_control_circuit_display0[5]));
  LED led_105 (.in(u_control_circuit_ground[5]));
  LED led_106 (.in(u_control_circuit_display5[4]));
  LED led_107 (.in(u_control_circuit_display4[4]));
  LED led_108 (.in(u_control_circuit_display3[4]));
  LED led_109 (.in(u_control_circuit_display2[4]));
  LED led_110 (.in(u_control_circuit_display1[4]));
  LED led_111 (.in(u_control_circuit_display0[4]));
  LED led_112 (.in(u_control_circuit_ground[4]));
  LED led_113 (.in(u_control_circuit_display5[3]));
  LED led_114 (.in(u_control_circuit_display4[3]));
  LED led_115 (.in(u_control_circuit_display3[3]));
  LED led_116 (.in(u_control_circuit_display2[3]));
  LED led_117 (.in(u_control_circuit_display1[3]));
  LED led_118 (.in(u_control_circuit_display0[3]));
  LED led_119 (.in(u_control_circuit_ground[3]));
  LED led_120 (.in(u_control_circuit_display5[2]));
  LED led_121 (.in(u_control_circuit_display4[2]));
  LED led_122 (.in(u_control_circuit_display3[2]));
  LED led_123 (.in(u_control_circuit_display2[2]));
  LED led_124 (.in(u_control_circuit_display1[2]));
  LED led_125 (.in(u_control_circuit_display0[2]));
  LED led_126 (.in(u_control_circuit_ground[2]));
  LED led_127 (.in(u_control_circuit_display5[1]));
  LED led_128 (.in(u_control_circuit_display4[1]));
  LED led_129 (.in(u_control_circuit_display3[1]));
  LED led_130 (.in(u_control_circuit_display2[1]));
  LED led_131 (.in(u_control_circuit_display1[1]));
  LED led_132 (.in(u_control_circuit_display0[1]));
  LED led_133 (.in(u_control_circuit_ground[1]));
  LED led_134 (.in(u_control_circuit_display5[0]));
  LED led_135 (.in(u_control_circuit_display4[0]));
  LED led_136 (.in(u_control_circuit_display3[0]));
  LED led_137 (.in(u_control_circuit_display2[0]));
  LED led_138 (.in(u_control_circuit_display1[0]));
  LED led_139 (.in(u_control_circuit_display0[0]));
  LED led_140 (.in(u_control_circuit_ground[0]));

  // Notes on the sheet:
  //   clk_2hz: Hz: 2
  //   clk_5hz: Hz: 5
  //   clk_10hz: Hz: 10
endmodule

/* Code of control_circuit:
library ieee;
use ieee.std_logic_1164.all;
use ieee.numeric_std.all;

entity control_circuit is	
	port	(
		-- Input ports
		clk_1hz, clk_2hz, clk_5hz, clk_10hz : in std_logic;
		start, jump, squat,replay : in std_logic;
		rand2, rand0 : in std_logic;	
		block_temp : in std_logic_vector(5 downto 0);
		-- Output ports
		time_signal : out std_logic_vector(5 downto 0);	
		q_signal : out std_logic_vector(5 downto 0);	
		ground : out std_logic_vector(19 downto 0);	
		display5, display4, display3, display2, display1, display0 : out std_logic_vector(19 downto 0);	
		player_display : out std_logic_vector(5 downto 0));
end control_circuit;

architecture control of control_circuit is	
	signal Q : integer := 0;
	signal Time : integer := 0; --遊戲執行的時間
	signal StartTime: integer:= 0; --遊戲開始後動畫停滯時間用--
	signal GameOverTime: integer:=0; --遊戲結束後動畫停滯時間用--
	signal Level : integer := 0;
	signal ground_signal: std_logic_vector(19 downto 0) := "00000000000000000000";
------------player signal-----------------------------------------------------
	signal pattern_jump : std_logic_vector(5 downto 0) := "011100";
	signal pattern_squat: std_logic_vector(5 downto 0) := "000001";
	signal pattern_start: std_logic_vector(5 downto 0) := "000111";
	signal pattern_reset: std_logic_vector(5 downto 0) := "000000";
------------block signal------------------------------------------------------
	signal block_2: std_logic_vector(19 downto 0) := "00000000000000000000";
	signal block_0: std_logic_vector(19 downto 0) := "00000000000000000000";
	signal block_zero: std_logic_vector(19 downto 0) := "00000000000000000000";
	signal crush : std_logic := '0';
------------game over display------------------------------------------------------
	signal gg5: std_logic_vector(19 downto 0) := "00001100000001100000";
	signal gg4: std_logic_vector(19 downto 0) := "00010000000010000000";
	signal gg3: std_logic_vector(19 downto 0) := "00010000000010000000";
	signal gg2: std_logic_vector(19 downto 0) := "00010111000010111000";
	signal gg1: std_logic_vector(19 downto 0) := "00010001000010001000";
	signal gg0: std_logic_vector(19 downto 0) := "00001101000001101000";
------------------------------------------------------------------------------
Begin
------------------display-----------------------------------------------------
display5 <= block_zero;
display4 <= block_zero;
display3 <= block_zero;
display2 <= block_2;
display1 <= block_zero;
display0 <= block_0;
ground <= ground_signal;
time_signal <= std_logic_vector(to_unsigned(time, 6));
q_signal <= std_logic_vector(to_unsigned(q, 6));
----------------player figures------------------------------------------------
	player_display <= pattern_jump when  (jump = '1') and (Q = 1 or  Q = 2 or  Q = 3 )
		else pattern_squat when (squat = '1') and (Q = 1 or  Q = 2 or  Q = 3 )
		else pattern_start when (squat = '0') and (jump = '0') and (Q = 1 or  Q = 2 or  Q = 3 )
		else pattern_reset;
----------------crush signal-------------------------------------------------
	crush <= (player_display(0) and block_temp(0))
		or (player_display(1) and block_temp(1))
		or (player_display(2) and block_temp(2))
		or (player_display(3) and block_temp(3))
		or (player_display(4) and block_temp(4))
		or (player_display(5) and block_temp(5));
------------------state control------------------------------------------------
process(clk_1hz, clk_2hz, clk_5hz, clk_10hz, Q) is
 	begin
 		if (Q = 0) and (start = '1') then --開機畫面待做
			if (rising_edge(clk_1hz)) then 
				StartTime <= StartTime + 1;
			end if;
			if(StartTime = 3) then  
				Q <= 1; StartTime <= 0; 
			end if;
		end if;

		if (Q = 1) then
			ground_signal <= "11111111111111111111";
			if (rising_edge(clk_1hz)) then 
				Time <= Time + 1;
			end if;
			if(Time = 25) then  
				Q <= 2; Time <= 0; 
			end if;
			if(crush = '1') then  
				Q <= 5; Time <= 0; 
			end if;
		end if;

		if (Q = 2) then
			ground_signal <= "11111111111111111111";
			if (rising_edge(clk_1hz)) then 
				Time <= Time + 1;
			end if;
			if(Time = 40) then  
				Q <= 3; Time <= 0; 
			end if;
			if(crush = '1') then  
				Q <= 5; Time <= 0; 
			end if;
		end if;

		if (Q = 3) then
			ground_signal <= "11111111111111111111";
			if (rising_edge(clk_1hz)) then 
				Time <= Time + 1;
			end if;
			if(Time = 60) then  
				Q <= 4; Time <= 0; 
			end if;
			if(crush = '1') then  
				Q <= 5; Time <= 0; 
			end if;
		end if;

		if (Q = 4) then
			ground_signal <= "11111111111111111111";
			if(crush = '1') then  
				Q <= 5; 
			end if;
		end if;

		if (Q = 5) then
			if (rising_edge(clk_1hz)) then 
				GameOverTime <= GameOverTime + 1;
			end if;
			if(GameOverTime > 2) then  --gg待做
				block_2 <= "00000000000000000000" ;
				block_0 <= "00000000000000000000" ;
				ground_signal <= "00000000000000000000";
			end if;
			if(Replay = '1') then  
				Q <= 0; GameOverTime <= 0; 
			end if;
		end if;
----------------block generator level1----------------------------------------
		if (rising_edge(clk_1hz)) and (Q = 1) then
			if (block_2(0) and rand2) or (block_0(0) and rand2)then
				block_2 <= block_2(18 downto 0) & "0";
			else block_2 <= block_2(18 downto 0) & rand2;
			end if;
			if (block_0(0) and rand0) or (block_2(0) and rand0) then
				block_0 <= block_0(18 downto 0) & "0";
			else block_0 <= block_0(18 downto 0) & rand0;
			end if;
		end if;
----------------block generator level2----------------------------------------
		if (rising_edge(clk_2hz)) and (Q = 2) then
			if (block_2(0) and rand2) or (block_0(0) and rand2)then
				block_2 <= block_2(18 downto 0) & "0";
			else block_2 <= block_2(18 downto 0) & rand2;
			end if;
			if (block_0(0) and rand0) or (block_2(0) and rand0) then
				block_0 <= block_0(18 downto 0) & "0";
			else block_0 <= block_0(18 downto 0) & rand0;
			end if;
		end if;
----------------block generator level3----------------------------------------
		if (rising_edge(clk_5hz)) and (Q = 3) then
			if (block_2(0) and rand2) or (block_0(0) and rand2)then
				block_2 <= block_2(18 downto 0) & "0";
			else block_2 <= block_2(18 downto 0) & rand2;
			end if;
			if (block_0(0) and rand0) or (block_2(0) and rand0) then
				block_0 <= block_0(18 downto 0) & "0";
			else block_0 <= block_0(18 downto 0) & rand0;
			end if;
		end if;
----------------block generator level4----------------------------------------
		if (rising_edge(clk_2hz)) and (Q = 10) then
			if (block_2(0) and rand2) or (block_0(0) and rand2)then
				block_2 <= block_2(18 downto 0) & "0";
			else block_2 <= block_2(18 downto 0) & rand2;
			end if;
			if (block_0(0) and rand0) or (block_2(0) and rand0) then
				block_0 <= block_0(18 downto 0) & "0";
			else block_0 <= block_0(18 downto 0) & rand0;
			end if;
		end if;
--------------------------------------------------------------------------------
end process;
end control;
*/
